# Fritzing sketch ladeschaltung_02 (saved by Fritzing 0.9.2b)
circuit board: 8.46667cm x 5.64444cm
breadboards: 1

parts:
  Q2_IRF9640 = Basic FET P-Channel [package="TO220 [THT]"]
  Q1_2N7000 = Basic FET N-Channel [package="TO220 [THT]"]
  R1 = Resistor [tolerance=±5% resistance=4.7k package=THT]
  R2 = Resistor [tolerance=±5% resistance=4.7k package=THT]
  R3 = Resistor [tolerance=±5% resistance=6 package=THT]
  U2 = LIPO-1000mAh [package=lipo-1000]
  R4 = Resistor [tolerance=±5% resistance=270 package=THT]
  R5 = Resistor [tolerance=±5% resistance=680 package=THT]
  R7 = Resistor [tolerance=±5% resistance=4.7k package=THT]
  Q3_BC307 = PNP-Transistor [package="TO92 [THT]"]
  U1_LM317T = Voltage Regulator [package=to220-adj]

nets:
  N1: Q2_IRF9640.gate, Q1_2N7000.drain, R2.Pin_0
  N2: Q2_IRF9640.drain, U1_LM317T.IN
  8V: Q2_IRF9640.source, R2.Pin_1
  N3: Q1_2N7000.gate, R1.Pin_1
  GND: Q1_2N7000.source, U2.-, R5.Pin_1
  dig input: R1.Pin_0, R7.Pin_1
  N4: R3.Pin_0, R4.Pin_0, U1_LM317T.OUT
  N5: R3.Pin_1, U2.+, Q3_BC307.C
  N6: R4.Pin_1, R5.Pin_0, Q3_BC307.E, U1_LM317T.ADJ
  N7: R7.Pin_0, Q3_BC307.B

notes:
  Strom- und Spannungsregelung
